# Fritzing sketch LegoControl2 (saved by Fritzing 0.9.3b)
breadboards: 1

parts:
  VCC1 = Battery block 9V
  Part2 = Bluetooth HC-05 Macho
  Port0 = Lego [package="SIP (Single Inline) [THT]"]
  Part3 = Arduino Pro Mini v13
  Port1 = Lego [package="SIP (Single Inline) [THT]"]
  Port2 = Lego [package="SIP (Single Inline) [THT]"]
  Port3 = Lego [package="SIP (Single Inline) [THT]"]

nets:
  GND: VCC1.-, Part2.GND, Port0.GND, Part3.GND, Port1.GND, Port2.GND, Port3.GND
  9V: VCC1.+, Port0.9V, Part3.RAW, Port1.9V, Port2.9V, Port3.9V
  N1: Part2.TXD, Part3.A2
  N2: Part2.RXD, Part3.A3
  VCC: Part2.VCC, Part3.VCC
  N3: Port0.C1, Part3.D10_PWM/SS
  N4: Port0.C2, Part3.A0
  N5: Part3.D12/MISO, Port2.C1
  N6: Part3.D11_PWM/MOSI, Port2.C2
  N7: Part3.D9_PWM, Port3.C2
  N8: Part3.D8, Port3.C1
  N9: Part3.D3_PWM, Port1.C2
  N10: Part3.D2, Port1.C1

custom parts:
  Lego: Lego Power Functions
